# Fritzing sketch wiring (saved by Fritzing 0.9.3b)
breadboards: 1

parts:
  C2 = Electrolytic Capacitor [capacitance=10µF package="100 mil [THT, electrolytic]"]
  R1 = Resistor [tolerance=±5% resistance=3.9k package="1206 [SMD]"]
  R3 = Resistor [tolerance=±5% resistance=1M package="1206 [SMD]"]
  BUS = Screw terminal - 2 pins [package=THT]
  Q1 = npn-Powertransistor [package="TO220 [THT]"]
  IC1 = WeMos D1 Mini ESP32
  C3 = Electrolytic Capacitor [capacitance=10µF voltage=20V package="100 mil [THT, electrolytic]"]
  R4 = Resistor [tolerance=±5% resistance=4.7k package="2512 [SMD]"]
  R5 = Resistor [tolerance=±5% resistance=100k package="2512 [SMD]"]
  D2 = Zener Diode [part_number=1N4728A breakdown_voltage=2V package="300 mil [THT]"]
  R6 = Resistor [tolerance=±5% resistance=100k package="2512 [SMD]"]
  Q2 = npn-Powertransistor [package="TO220 [THT]"]
  R7 = Resistor [tolerance=±5% resistance=4.7k package="1206 [SMD]"]
  R8 = Resistor [tolerance=±5% resistance=200k package="1206 [SMD]"]
  Q3 = NPN-Transistor [package="TO92 [THT]"]
  Q4 = NPN-Transistor [package="TO92 [THT]"]
  R13 = Resistor [tolerance=±5% resistance=820 package=THT]
  R14 = Resistor [tolerance=±5% resistance=10k package=THT]
  R15 = Resistor [tolerance=±5% resistance=82k package=THT]
  C4 = Ceramic Capacitor [capacitance=100nF voltage=63V package="100 mil [THT, multilayer]"]
  C5 = Ceramic Capacitor [capacitance=1nF voltage=63V package="100 mil [THT, multilayer]"]
  R16 = Resistor [tolerance=±5% resistance=39 package="2010 [SMD]"]
  TM1_4_7k = TRIMPOT [package=trimpot-3mm]
  R18 = Resistor [tolerance=±5% resistance=22k package=THT]
  R26 = Resistor [tolerance=±5% resistance=2.2k package=THT]
  R27 = Resistor [tolerance=±5% resistance=1k package=THT]
  Q9 = NPN-Transistor [package="TO92 [THT]"]

nets:
  N1: C2.-, IC1.IO18
  N2: C2.+, R1.Pin_1, Q1.base
  GND: R1.Pin_0, BUS.pin2, Q1.emitter, IC1.G, D2.anode, R6.Pin_1, Q2.emitter, R8.Pin_0, R27.Pin_1, Q9.C
  N3: R3.Pin_0, BUS.pin1, Q1.collector, C3.+, R8.Pin_1, R13.Pin_1
  N4: R3.Pin_1, Q2.base
  3.3V: IC1.3V3, R5.Pin_0, R7.Pin_1
  N5: IC1.SVP, R4.Pin_1, R5.Pin_1, D2.cathode, R6.Pin_0
  N6: IC1.IO5, Q2.collector, R7.Pin_0
  N7: C3.-, R4.Pin_0
  N8: Q3.E, R16.Pin_0, TM1_4_7k.CW, Q9.E
  N9: Q3.B, R14.Pin_1, R15.Pin_0, C5.0
  N10: Q3.C, Q4.B, R18.Pin_0
  N11: Q4.E, R15.Pin_1, C5.1, R16.Pin_1
  N12: Q4.C, R13.Pin_0
  N13: R14.Pin_0, C4.1
  N14: C4.0, TM1_4_7k.WIPER
  IO25: TM1_4_7k.CCW
  5V: R18.Pin_1
  N15: R26.Pin_0, R27.Pin_0, Q9.B
  IO15: R26.Pin_1
